// Digital circuit 4_bit_adder.dig as structural Verilog
module _4_bit_adder (
  input  A0__LSB,
  input  B0,
  input  C0,
  input  D0,
  input  Carry_In,
  input  A1__LSB,
  input  B1,
  input  C1,
  input  D1,
  output A__LSB,
  output B,
  output C,
  output D,
  output Carry_Out
);

  wire full_adder_1_carry, full_adder_2_carry, full_adder_3_carry;

  full_adder full_adder_1 (.A(Carry_In), .B(A0__LSB), .C(A1__LSB), .Sum(A__LSB), .Carry(full_adder_1_carry));
  full_adder full_adder_2 (.A(full_adder_1_carry), .B(B0), .C(B1), .Sum(B), .Carry(full_adder_2_carry));
  full_adder full_adder_3 (.A(full_adder_2_carry), .B(C0), .C(C1), .Sum(C), .Carry(full_adder_3_carry));
  full_adder full_adder_4 (.A(full_adder_3_carry), .B(D0), .C(D1), .Sum(D), .Carry(Carry_Out));
endmodule
