// Digital circuit 4_bit_adder_comp.dig as structural Verilog
module _4_bit_adder_comp (
  input  [3:0] B,
  input  Carry_In,
  input  [3:0] A,
  output [3:0] Out,
  output Carry_Out
);

  _4_bit_adder _4_bit_adder_1 (
    .A0__LSB(A[0]), .B0(A[1]), .C0(A[2]), .D0(A[3]), .Carry_In(Carry_In), .A1__LSB(B[0]), .B1(B[1]),
    .C1(B[2]), .D1(B[3]), .A__LSB(Out[0]), .B(Out[1]), .C(Out[2]), .D(Out[3]), .Carry_Out(Carry_Out));
  // Pins of 1 and 4 bits meet at B
  // Pins of 1 and 4 bits meet at A
  // Pins of 1 and 4 bits meet at Out
endmodule
