// Digital circuit 4_bit_mux.dig as structural Verilog
module _4_bit_mux (
  input  A0__LSB,
  input  B0,
  input  C0,
  input  D0,
  input  A1__LSB,
  input  B1,
  input  C1,
  input  D1,
  input  Control,
  output A__LSB,
  output B,
  output C,
  output D
);

  mux mux_1 (.A(A0__LSB), .B(A1__LSB), .C(Control), .Out(A__LSB));
  mux mux_2 (.A(B0), .B(B1), .C(Control), .Out(B));
  mux mux_3 (.A(C0), .B(C1), .C(Control), .Out(C));
  mux mux_4 (.A(D0), .B(D1), .C(Control), .Out(D));
endmodule
