// Digital circuit 4_bit_mux_comp.dig as structural Verilog
module _4_bit_mux_comp (
  input  [3:0] A,
  input  [3:0] B,
  input  Control,
  output [3:0] Out
);

  _4_bit_mux _4_bit_mux_1 (
    .A0__LSB(A[0]), .B0(A[1]), .C0(A[2]), .D0(A[3]), .A1__LSB(B[0]), .B1(B[1]), .C1(B[2]), .D1(B[3]),
    .Control(Control), .A__LSB(Out[0]), .B(Out[1]), .C(Out[2]), .D(Out[3]));
endmodule
