// Digital circuit 4_bit_register.dig as structural Verilog
module _4_bit_register (
  input  WN,
  input  IA__LSB,
  input  IB,
  input  IC,
  input  ID,
  output A__LSB,
  output B,
  output C,
  output D
);

  register register_1 (.Set(WN), .Data(IA__LSB), .Out(A__LSB));
  register register_2 (.Set(WN), .Data(IB), .Out(B));
  register register_3 (.Set(WN), .Data(IC), .Out(C));
  register register_4 (.Set(WN), .Data(ID), .Out(D));
endmodule
