// Digital circuit 4_bit_register_comp.dig as structural Verilog
module _4_bit_register_comp (
  input  [3:0] Data,
  input  WN,
  output [3:0] Out
);

  _4_bit_register _4_bit_register_1 (
    .WN(WN), .IA__LSB(Data[0]), .IB(Data[1]), .IC(Data[2]), .ID(Data[3]), .A__LSB(Out[0]), .B(Out[1]),
    .C(Out[2]), .D(Out[3]));
endmodule
