// Digital circuit cpu.dig as structural Verilog
module cpu (
  input  [7:0] Instruction,
  output [3:0] Register_C,
  output [3:0] Register_B,
  output [3:0] Register_A
);

  wire _4_bit_adder_comp_1_p4;
  wire [3:0] _4_bit_mux_comp_1_out;

  _4_bit_mux_comp _4_bit_mux_comp_1 (
    .A(Instruction[7:4]), .B(Register_C), .Control(Instruction[3]), .Out(_4_bit_mux_comp_1_out));
  _4_bit_register_comp _4_bit_register_comp_1 (.Data(_4_bit_mux_comp_1_out), .WN(Instruction[0]), .Out(Register_A));
  // _4_bit_adder_comp _4_bit_adder_comp_1: pin names not known; wires that end beside it: Register_A, 1'b0, Register_B, _4_bit_adder_comp_1_p4
  // _4_bit_register_comp _4_bit_register_comp_2: pin names not known; wires that end beside it: Instruction[2], Register_C, _4_bit_adder_comp_1_p4
  Seven_Seg_Hex seven_seg_hex_1 (.d(Register_C), .dp(1'b0));
  _4_bit_register_comp _4_bit_register_comp_3 (.Data(_4_bit_mux_comp_1_out), .WN(Instruction[1]), .Out(Register_B));
endmodule
