// Digital circuit demux.dig as structural Verilog
module demux (
  input  A,
  input  C,
  output A_2,
  output B
);

  wire not_1_out;

  not not_1 (not_1_out, C);
  and and_1 (A_2, A, not_1_out);
  and and_2 (B, A, C);
endmodule
