// Digital circuit full_adder.dig as structural Verilog
module full_adder (
  input  A,
  input  B,
  input  C,
  output Sum,
  output Carry
);

  wire and_1_out, and_2_out, and_3_out, xor_1_out;

  and and_1 (and_1_out, A, B);
  and and_2 (and_2_out, A, C);
  xor xor_1 (xor_1_out, A, B);
  and and_3 (and_3_out, B, C);
  xor xor_2 (Sum, xor_1_out, C);
  or or_1 (Carry, and_3_out, and_2_out, and_1_out);
endmodule
