// Digital circuit main.dig as structural Verilog
module main (
  input  clk,
  input  Power
);

  wire Reset_out;
  wire [3:0] counter_1_out, cpu_1_register_a, cpu_1_register_b, cpu_1_register_c;
  wire [7:0] rom_1_d;

  Button Reset (.out(Reset_out));
  Counter #(.Bits(4)) counter_1 (.en(Power), .C(clk), .clr(Reset_out), .out(counter_1_out));  // open: ovf
  ROM #(.AddrBits(4), .Bits(8)) rom_1 (.A(counter_1_out), .sel(1'b1), .D(rom_1_d));
  cpu cpu_1 (
    .Instruction(rom_1_d), .Register_C(cpu_1_register_c), .Register_B(cpu_1_register_b),
    .Register_A(cpu_1_register_a));
  Seven_Seg_Hex seven_seg_hex_1 (.d(cpu_1_register_a), .dp(1'b0));
  Seven_Seg_Hex seven_seg_hex_2 (.d(cpu_1_register_b), .dp(1'b0));
  Seven_Seg_Hex seven_seg_hex_3 (.d(cpu_1_register_c), .dp(1'b0));

  // Notes on the sheet:
  //   contents of rom_1 (hex, n*v repeats v):
  //   1,12,c,9,c,a,c,9,c,a,c,9,c,a
  //   Register A
  //   Register B
  //   Register C
endmodule
