// Digital circuit register.dig as structural Verilog
module register (
  input  Set,
  input  Data,
  output Out
);

  wire nand_1_out, nand_2_out, nand_4_out, not_1_out;

  not not_1 (not_1_out, Data);
  nand nand_1 (nand_1_out, Set, Data);
  nand nand_2 (nand_2_out, Set, not_1_out);
  nand nand_3 (Out, nand_1_out, nand_4_out);
  nand nand_4 (nand_4_out, Out, nand_2_out);
endmodule
